# Fritzing sketch setup (saved by Fritzing 0.9.3b)
breadboards: 1

parts:
  NEOPIXEL = Neopixel Strip -- Black (30/m)
  Arduino_Uno = Arduino Uno (Rev3)
  Resistor = Resistor [tolerance=±5% resistance=330 package=THT]
  Load_Cell = Load Cell - Red/white/black/green
  Part4 = HX711 Weighing Sensor Module
  5v_Power_Source = DC-DC Power Module (5v)

nets:
  N1: NEOPIXEL.+5V, 5v_Power_Source.Vout
  N2: NEOPIXEL.DI, Resistor.Pin_1
  GND: NEOPIXEL.GND, Part4.GND, 5v_Power_Source.GND*
  N3: Arduino_Uno.D11_PWM/MOSI, Resistor.Pin_0
  N4: Arduino_Uno.D4, Part4.DO/RX
  N5: Arduino_Uno.D5_PWM, Part4.CK/TX
  N6: Load_Cell.wire1, Part4.E+
  N7: Load_Cell.wire2, Part4.A+
  N8: Load_Cell.wire3, Part4.E-
  N9: Load_Cell.wire4, Part4.A-

notes:
  5v External power source
  LED strip
  Weight cell

custom parts:
  Neopixel Strip -- Black (30/m): Neopixel Strip, Black, 30 pixels per meter.
  Load Cell - Red/white/black/green: A rectangle load cell/weighting pressure Sensor with four wires - Red, white, black, green. Normally corresponding with E+, E-, A+, A- respectively.
  HX711 Weighing Sensor Module: HX711 is a precision 24-bit analog-to-digital converter (ADC) designed for weigh scales and industrial control applications to interface directly with a bridge sensor.
  DC-DC Power Module (5v): DC-DC Power Module based con AMS1117-5.0 Input: DC 6~12V (input power must higher 1V than output power); Output: 5V (+/-0.05V error), 800mA
